# Fritzing sketch DCC-Encoder-Throttle (saved by Fritzing 0.9.3b)
circuit board: 8cm x 8cm
breadboards: 1

parts:
  RE1 = Rotary Encoder [package=THT]
  J1 = female pin header, 2 pins [form="♀ (female)"]
  J2 = female pin header, 4 pins [form="♀ (female)"]
  Nano = Arduino Nano (Rev3.0)
  U1 = LCD-16X2 [package=lcd-16x2]  # not connected
  C1 = Ceramic Capacitor [capacitance=100nF package="100 mil [THT, multilayer]"]
  C2 = Ceramic Capacitor [capacitance=100nF package="100 mil [THT, multilayer]"]
  R1 = Resistor [tolerance=±5% power=0.25 resistance=10k package=THT]
  J3 = female pin header, 10 pins [form="♀ (female)"]
  J4 = female pin header, 4 pins [form="♀ (female)"]

nets:
  N1: RE1.EncoderPinA, Nano.D2, C1.1
  N2: RE1.EncoderPinC, J1.pin1, J2.pin1, Nano.GND, C1.0, C2.1, J4.pin2
  N3: RE1.EncoderPinB, Nano.D3, C2.0
  N4: J1.pin2, Nano.D4, R1.Pin_0
  N5: J2.pin2, Nano.5V, R1.Pin_1, J4.pin1
  N6: J2.pin3, Nano.A5
  N7: J2.pin4, Nano.A4
  N8: Nano.D1/TX, J4.pin4
  N9: Nano.D0/RX, J4.pin3
  N10: Nano.D5, J3.pin1
  N11: Nano.D6, J3.pin2
  N12: Nano.D7, J3.pin3
  N13: Nano.D8, J3.pin4
  N14: Nano.D9, J3.pin5
  N15: Nano.D10, J3.pin6
  N16: Nano.D11/MOSI, J3.pin7
  N17: Nano.D12/MISO, J3.pin8

notes:
  +
  -
  RX
  TX
